# Fritzing sketch ArduinoBluetoothCarControl (saved by Fritzing 0.9.0b)
breadboards: 1

parts:
  부품1 = Arduino Ethernet Shield (Rev3)
  M1 = DC Motor
  M2 = DC Motor
  부품6 = Bluetooth Mate Silver  # not connected
  VCC1 = Battery  # not connected
  IC1 = L293D [package=THT]

nets:
  N1: 부품1.PWM_D9, IC1.Enable_1
  N2: 부품1.ETH_CS, IC1.Enable_2
  N3: 부품1.D2, IC1.In_2
  N4: 부품1.PWM_D3, IC1.In_1
  N5: 부품1.SDCS, IC1.In_3
  N6: 부품1.PWM_D5, IC1.In_4
  N7: 부품1.5V, IC1.+V
  N8: 부품1.GND, IC1.0V
  N9: 부품1.VIN, IC1.+Vmotor
  N10: M1.pin_1, IC1.Out_3_(_Controlled_by_Enable_2_)
  N11: M1.pin_2, IC1.Out_4_(_Controlled_by_Enable_2_)
  N12: M2.pin_1, IC1.Out_2_(_Controlled_by_Enable_1_)
  N13: M2.pin_2, IC1.Out_1_(_Controlled_by_Enable_1_)

notes:
  <--Bluetooth Slave UART Board
  EN VCC GND TXD RXD STATE
  x * * * * x
  Arduino Bluetooth Car Control Project
