# Fritzing sketch smart_home (saved by Fritzing 0.9.0b)
breadboards: 1

parts:
  LED1 = LED - 5mm [color="Red (633nm)" package="5 mm [THT]"]
  R1 = Resistor [tolerance=±5% resistance=220 package=THT]
  부품1 = Arduino Uno (Rev3)
  S2 = Pushbutton [package=THT]
  R2 = Resistor [tolerance=±5% resistance=220 package=THT]
  RHT1 = Humidity and Temperature Sensor RHT03
  Q1 = NPN-Transistor [package="TO92 [THT]"]
  M1 = DC Motor
  R3 = Photocell (LDR) [package=THT]
  R4 = Resistor [tolerance=±5% resistance=220 package=THT]
  J1 = Basic Servo
  J2 = Infrared Proximity Sensor
  MIC1 = Microphone

nets:
  N1: LED1.cathode, R2.Pin_1, RHT1.GND_2, Q1.E
  N2: LED1.anode, R1.Pin_0
  N3: R1.Pin_1, 부품1.D2
  N4: 부품1.A0, R3.pin_0, R4.Pin_1
  N5: 부품1.D8, Q1.C
  N6: 부품1.D11_PWM/MOSI, J2.GND
  N7: 부품1.D12/MISO, J2.Vout
  N8: 부품1.D3_PWM, J1.pulse
  N9: 부품1.D4, S2.leg0, R2.Pin_0
  N10: 부품1.D5_PWM, MIC1.pin2
  N11: 부품1.D7, RHT1.Data-signal
  N12: S2.leg1, RHT1.Vcc, M1.pin_1
  N13: Q1.B, M1.pin_2
  VCC: R3.pin_1, J1.vcc, J2.Vcc
  N14: R4.Pin_0, J1.gnd, MIC1.pin1
